# Fritzing sketch 64 Channel Driver Sketch (saved by Fritzing 0.9.1b)
circuit board: 11.9361cm x 7.44329cm
breadboards: 2

parts:
  U1 = 74HC595 [package="DIP16 [THT]"]
  IC1 = ULN2803A [package=THT]
  U2 = 74HC595 [package="DIP16 [THT]"]
  IC2 = ULN2803A [package=THT]
  U4 = 74HC595 [package="DIP16 [THT]"]
  U3 = 74HC595 [package="DIP16 [THT]"]
  IC4 = ULN2803A [package=THT]
  IC3 = ULN2803A [package=THT]
  X1 = DB9 Connector [package=db9]
  X2 = DB9 Connector [package=db9]
  X3 = DB9 Connector [package=db9]
  X4 = DB9 Connector [package=db9]
  JP2 = Header 3 [package=molex-1x3_lock]
  JP1 = Header 2 [package=molex-1x2_lock]

nets:
  N1: U1.Q1, IC1.In_7
  N2: U1.Q2, IC1.In_6
  N3: U1.Q3, IC1.In_5
  N4: U1.Q4, IC1.In_4
  N5: U1.Q5, IC1.In_3
  N6: U1.Q6, IC1.In_2
  N7: U1.Q7, IC1.In_1
  GND: U1.GND, U1.OE, IC1.0V, U2.GND, U2.OE, IC2.0V, U4.GND, U4.OE, U3.GND, U3.OE, IC4.0V, IC3.0V, X1.5, X2.5, X3.5, X4.5, JP1.2
  N8: U1.Q7', U2.DS
  VCC: U1.MR, U1.VCC, IC1.COM_-_Common, U2.MR, U2.VCC, IC2.COM_-_Common, U4.MR, U4.VCC, U3.MR, U3.VCC, IC4.COM_-_Common, IC3.COM_-_Common, JP1.1
  N9: U1.SH_CP, U2.SH_CP, U4.SH_CP, U3.SH_CP, JP2.3
  N10: U1.ST_CP, U2.ST_CP, U4.ST_CP, U3.ST_CP, JP2.2
  N11: U1.DS, JP2.1
  N12: U1.Q0, IC1.In_8
  N13: IC1.Out_8, X1.1
  N14: IC1.Out_7, X1.2
  N15: IC1.Out_6, X1.3
  N16: IC1.Out_5, X1.4
  N17: IC1.Out_4, X1.6
  N18: IC1.Out_3, X1.7
  N19: IC1.Out_2, X1.8
  N20: IC1.Out_1, X1.9
  N21: U2.Q1, IC2.In_7
  N22: U2.Q2, IC2.In_6
  N23: U2.Q3, IC2.In_5
  N24: U2.Q4, IC2.In_4
  N25: U2.Q5, IC2.In_3
  N26: U2.Q6, IC2.In_2
  N27: U2.Q7, IC2.In_1
  N28: U2.Q7', U3.DS
  N29: U2.Q0, IC2.In_8
  N30: IC2.Out_8, X2.1
  N31: IC2.Out_7, X2.2
  N32: IC2.Out_6, X2.3
  N33: IC2.Out_5, X2.4
  N34: IC2.Out_4, X2.6
  N35: IC2.Out_3, X2.7
  N36: IC2.Out_2, X2.8
  N37: IC2.Out_1, X2.9
  N38: U4.Q1, IC4.In_7
  N39: U4.Q2, IC4.In_6
  N40: U4.Q3, IC4.In_5
  N41: U4.Q4, IC4.In_4
  N42: U4.Q5, IC4.In_3
  N43: U4.Q6, IC4.In_2
  N44: U4.Q7, IC4.In_1
  N45: U4.DS, U3.Q7'
  N46: U4.Q0, IC4.In_8
  N47: U3.Q1, IC3.In_7
  N48: U3.Q2, IC3.In_6
  N49: U3.Q3, IC3.In_5
  N50: U3.Q4, IC3.In_4
  N51: U3.Q5, IC3.In_3
  N52: U3.Q6, IC3.In_2
  N53: U3.Q7, IC3.In_1
  N54: U3.Q0, IC3.In_8
  N55: IC4.Out_8, X4.1
  N56: IC4.Out_7, X4.2
  N57: IC4.Out_6, X4.3
  N58: IC4.Out_5, X4.4
  N59: IC4.Out_4, X4.6
  N60: IC4.Out_3, X4.7
  N61: IC4.Out_2, X4.8
  N62: IC4.Out_1, X4.9
  N63: IC3.Out_8, X3.1
  N64: IC3.Out_7, X3.2
  N65: IC3.Out_6, X3.3
  N66: IC3.Out_5, X3.4
  N67: IC3.Out_4, X3.6
  N68: IC3.Out_3, X3.7
  N69: IC3.Out_2, X3.8
  N70: IC3.Out_1, X3.9
